# Fritzing sketch circuit (saved by Fritzing 0.9.7b)
breadboards: 1

parts:
  Part1 = Adafruit Trinket M0 [part_number="Adafruit #3500"]
  T1 = TMP36 Temperature Sensor [package="TO92 [THT]"]
  Part2 = OLED Monochrome 128x32 I2C [part_number=931]

nets:
  GND: Part1.GND, T1.GND, Part2.GND
  N1: Part1.D4_A2_PA06_TXD_MOSI, T1.Vout
  3.3V: Part1.3.3V, T1.+Vs, Part2.3.3V
  N2: Part1.D2_A1_PA09_SCL_MISO, Part2.SCL
  N3: Part1.D0_A4_PA08_SDA, Part2.SDA

custom parts:
  OLED Monochrome 128x32 I2C: These displays are small, only about 1" diagonal, but very readable due to the high contrast of an OLED display. This display is made of 128x32 individual white OLED pixels, each one is turned on or off by the controller chip. Because the display makes its own light, no backlight is required. This reduces the power required to run the OLED and is why the display has such high contrast; we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
